# Fritzing sketch AlcoholSensor (saved by Fritzing 0.6.5b)
breadboards: 1

parts:
  Part1 = Gas Sensor Breakout Board
  U1 = Voltage Regulator - 5V [package="TO220 [THT]"]
  VCC1 = Battery block 9V
  R1 = Resistor [tolerance=±5% resistance=10k package=THT]
  Arduino1 = Arduino
  U2 = mystery part, 3 pins [chip_label="4 digit 7 seg led display" spacing=300mil]

nets:
  N1: Part1.A1, Part1.H1, U1.output_voltage
  GND: Part1.GND, U1.GND, VCC1.-, R1.Pin_0, Arduino1.GND, U2.pin2
  N2: Part1.B1, R1.Pin_1, Arduino1.A0
  N3: U1.input_voltage, VCC1.+
  N4: Arduino1.+5V, U2.pin1
  N5: Arduino1.A1, U2.pin3
