# Fritzing sketch BoozeSensor (saved by Fritzing 0.7.11b)
perfboards: 1

parts:
  Part1 = Gas Sensor Breakout Board  # not connected
  R1 = Temperature Sensor (Thermistor) [thermistor_type=NTC package=THT]
  J1 = Generic male header - 6 pins [package=THT]
  J2 = Generic male header - 2 pins [package=THT]
  J3 = Generic male header - 2 pins [package=THT]
  Q1 = NPN-Transistor [package="TO92 [THT]"]
  R3 = 10k Ω Resistor [package=THT]
  R2 = 1k Ω Resistor [package=THT]
  R1_2 = 10k Ω Resistor [package=THT]

nets:
  N1: R1.pin_0, J1.pin5, R1_2.Pin_0
  N2: R1.pin_1, J3.pin1, J3.pin2
  N3: J1.pin2, R2.Pin_1
  N4: J2.pin1, R3.Pin_0
  N5: J2.pin2, Q1.collector
  N6: Q1.emitter, R3.Pin_1, R1_2.Pin_1
  N7: Q1.base, R2.Pin_0

notes:
  black: GND
  yellow: base (control)
  blue: alc. level
  purple: therm level
  red: 5V
  orange: emitter
  grey: collector
