# Fritzing sketch prototype (saved by Fritzing 0.7.11b)
breadboards: 2

parts:
  Arduino1 = Arduino
  Part1 = Gas Sensor Breakout Board
  Q1 = NPN-Transistor [package="TO92 [THT]"]
  Q2 = NPN-Transistor [package="TO92 [THT]"]
  S1 = Pushbutton [package="[THT]"]
  S2 = Pushbutton [package="[THT]"]
  S3 = Pushbutton [package="[THT]"]
  therm = 7-Segment Serial Display (Sparkfun COM-1144x, COM-11629) [part_number=COM-1144x]
  J1 = Piezo Speaker
  LED1 = RGB LED (com. cathode, rgb) [package="5 mm [THT]"]
  R1 = Resistor [tolerance=±5% resistance=10k package=THT]
  R2 = Resistor [tolerance=±5% resistance=10k package=THT]
  R3 = Resistor [tolerance=±5% resistance=10k package=THT]
  R4 = Resistor [tolerance=±5% resistance=150 package=THT]
  R5 = Resistor [tolerance=±5% resistance=100 package=THT]
  R6 = Resistor [tolerance=±5% resistance=100 package=THT]
  LED2 = LED - 5mm [color="Blue (525nm)" package="5 mm [THT]"]
  R8 = Resistor [tolerance=±5% resistance=1k package=THT]
  R9 = Resistor [tolerance=±5% resistance=100 package=THT]
  R10 = Resistor [tolerance=±5% resistance=10k package=THT]
  LED3 = LED - 3mm [color="Green (570nm)" package="3 mm [THT]"]
  R11 = Resistor [tolerance=±5% resistance=220 package=THT]
  C1 = Ceramic Capacitor [capacitance=100nF part_number=thermistor package="100 mil [THT, multilayer]"]
  R12 = Resistor [tolerance=±5% resistance=150 package=THT]

nets:
  GND: Arduino1.GND, Q1.E, Q2.E, therm.GND, LED1.common_cathode, R1.Pin_0, R2.Pin_0, R3.Pin_0, R9.Pin_1, R12.Pin_1
  N1: Arduino1.D13, Q1.B
  N2: Arduino1.D11, R4.Pin_1
  N3: Arduino1.D10, R5.Pin_1
  N4: Arduino1.D9, R6.Pin_1
  N5: Arduino1.D7, LED2.anode, R8.Pin_1
  N6: Arduino1.D4, S3.Pin_3, S3.Pin_4, R1.Pin_1
  N7: Arduino1.D3, S2.Pin_3, S2.Pin_4, R2.Pin_1
  N8: Arduino1.D2, S1.Pin_3, S1.Pin_4, R3.Pin_1
  +5V: Arduino1.+5V, Part1.H1, Part1.A1, S1.Pin_1, S1.Pin_2, S2.Pin_1, S2.Pin_2, S3.Pin_1, S3.Pin_2, therm.VCC, J1.pin2, LED3.anode, C1.0
  N9: Arduino1.A4, C1.1, R12.Pin_0
  N10: Arduino1.A5, Part1.B1, R10.Pin_0
  N11: Part1.GND, Q2.C
  N12: Q1.C, J1.pin1, R11.Pin_1
  N13: Q2.B, R8.Pin_0
  N14: LED1.red_anode, R4.Pin_0
  N15: LED1.green_anode, R5.Pin_0
  N16: LED1.blue_anode, R6.Pin_0
  N17: LED2.cathode, R9.Pin_0

notes:
  FAN

custom parts:
  7-Segment Serial Display (Sparkfun COM-1144x, COM-11629): Description: The 7-Segment Serial Display combines a classic 4-digit 7-segment display and an ATMega328 microcontroller allowing you to control every segment individually using only a few serial lines. It can be controlled in one of three ways: Serial TTL communication, SPI serial communication or I2C serial. You can even program it for stand-alone operation since the ATMega328 comes pre-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
