# Fritzing sketch LightOrgan (saved by Fritzing 0.7.12b)
breadboards: 2

parts:
  C1 = Electrolytic Capacitor [capacitance=0.1mF package="100 mil [THT, electrolytic]"]
  U1 = Voltage Regulator - 5V [package="TO220 [THT]"]
  C2 = Electrolytic Capacitor [capacitance=1µF package="100 mil [THT, electrolytic]"]
  J1 = Screw terminal - 2 pins [part_number="PWR IN" package=THT]
  Y1 = Resonator [frequency="16 Mhz" package=THT]
  U2 = atmega168 [package=dip]
  C3 = Ceramic Capacitor [capacitance=100nF package="100 mil [THT, multilayer]"]
  J2 = female pin header, 6 pins [form="♀ (female)"]
  S1 = Pushbutton [package="[THT]"]
  C4 = Ceramic Capacitor [capacitance=100nF package="100 mil [THT, multilayer]"]
  R1 = Resistor [tolerance=±5% resistance=10k package=THT]
  IC1 = IC, DIP package, 28 pins [chip_label=IC]
  IC2 = IC, DIP package, 28 pins [chip_label=IC]
  R2 = Resistor [tolerance=±5% resistance=2.2k package=THT]
  R3 = Resistor [tolerance=±5% resistance=2.2k package=THT]
  LED1 = RGB LED (com. anode, rbg) [package="5 mm [THT]"]
  LED2 = RGB LED (com. anode, rbg) [package="5 mm [THT]"]
  IC3 = IC, DIP package, 28 pins [chip_label=IC]
  LED12 = RGB LED (com. anode, rbg) [package="5 mm [THT]"]
  LED14 = RGB LED (com. anode, rbg) [package="5 mm [THT]"]
  LED15 = RGB LED (com. anode, rbg) [package="5 mm [THT]"]
  LED16 = RGB LED (com. anode, rbg) [package="5 mm [THT]"]
  LED17 = RGB LED (com. anode, rbg) [package="5 mm [THT]"]
  LED18 = RGB LED (com. anode, rbg) [package="5 mm [THT]"]
  LED19 = RGB LED (com. anode, rbg) [package="5 mm [THT]"]
  LED20 = RGB LED (com. anode, rbg) [package="5 mm [THT]"]
  LED21 = RGB LED (com. anode, rbg) [package="5 mm [THT]"]
  LED22 = RGB LED (com. anode, rbg) [package="5 mm [THT]"]
  LED23 = RGB LED (com. anode, rbg) [package="5 mm [THT]"]
  LED24 = RGB LED (com. anode, rbg) [package="5 mm [THT]"]
  LED25 = RGB LED (com. anode, rbg) [package="5 mm [THT]"]
  LED26 = RGB LED (com. anode, rbg) [package="5 mm [THT]"]
  R4 = Resistor [tolerance=±5% resistance=2.2k package=THT]
  R5 = Resistor [tolerance=±5% resistance=10k package=THT]

nets:
  N1: C1.-, U2.GND, C3.1, J2.pin6, IC1.pin22, IC1.pin27, IC2.pin22, IC2.pin27, R2.Pin_0, R3.Pin_0, IC3.pin22, IC3.pin27, R4.Pin_0, R5.Pin_0
  N2: C1.+, U1.output_voltage, U2.VCC, U2.AVCC, U2.AREF, C3.0, J2.pin4, R1.Pin_1, IC1.pin19, IC1.pin21, IC2.pin19, IC2.pin21, LED1.common_anode, LED2.common_anode, IC3.pin19, IC3.pin21, LED12.blue_cathode, LED14.common_anode, LED15.common_anode, LED16.common_anode, LED17.common_anode, LED18.common_anode, LED19.common_anode, LED20.common_anode, LED21.common_anode, LED22.common_anode, LED23.common_anode, LED24.common_anode, LED25.common_anode, LED26.common_anode
  N3: U1.input_voltage, C2.+, J1.pin1
  N4: U1.GND, C2.-, J1.pin2
  N5: Y1.0, U2.XLAT2
  N6: Y1.pin_1, U2.XLAT1
  N7: U2.RESET, J2.pin1, S1.Pin_1, S1.Pin_2, C4.1, R1.Pin_0
  N8: U2.D0_(RX), J2.pin2
  N9: U2.D1_(TX), J2.pin3
  N10: U2.D3_(PWM), IC1.pin18, IC2.pin18, IC3.pin18
  N11: U2.D9_(PWM), IC1.pin24, IC2.pin24, IC3.pin24
  N12: U2.D10_(PWM), IC1.pin23, IC2.pin23, IC3.pin23, R5.Pin_1
  N13: U2.D11_(PWM), IC3.pin26
  N14: U2.D13, IC1.pin25, IC2.pin25, IC3.pin25
  N15: S1.Pin_3, S1.Pin_4
  N16: IC1.pin1, LED16.green_cathode
  N17: IC1.pin2, LED16.blue_cathode
  N18: IC1.pin3, LED16.red_cathode
  N19: IC1.pin4, LED14.green_cathode
  N20: IC1.pin5, LED14.blue_cathode
  N21: IC1.pin6, LED14.red_cathode
  N22: IC1.pin7, LED2.green_cathode
  N23: IC1.pin8, LED2.blue_cathode
  N24: IC1.pin9, LED2.red_cathode
  N25: IC1.pin10, LED12.green_cathode
  N26: IC1.pin11, LED12.common_anode
  N27: IC1.pin12, LED12.red_cathode
  N28: IC1.pin13, LED1.green_cathode
  N29: IC1.pin14, LED1.blue_cathode
  N30: IC1.pin15, LED1.red_cathode
  N31: IC1.pin20, R2.Pin_1
  N32: IC1.pin26, IC2.pin17
  N33: IC1.pin28, LED17.red_cathode
  N34: IC2.pin1, LED22.red_cathode
  N35: IC2.pin2, LED21.green_cathode
  N36: IC2.pin3, LED21.blue_cathode
  N37: IC2.pin4, LED21.red_cathode
  N38: IC2.pin5, LED20.green_cathode
  N39: IC2.pin6, LED20.blue_cathode
  N40: IC2.pin7, LED20.red_cathode
  N41: IC2.pin8, LED19.green_cathode
  N42: IC2.pin9, LED19.blue_cathode
  N43: IC2.pin10, LED19.red_cathode
  N44: IC2.pin11, LED18.green_cathode
  N45: IC2.pin12, LED18.blue_cathode
  N46: IC2.pin13, LED18.red_cathode
  N47: IC2.pin14, LED17.green_cathode
  N48: IC2.pin15, LED17.blue_cathode
  N49: IC2.pin20, R4.Pin_1
  N50: IC2.pin26, IC3.pin17
  N51: IC2.pin28, LED22.blue_cathode
  N52: R3.Pin_1, IC3.pin20
  N53: IC3.pin1, LED15.blue_cathode
  N54: IC3.pin2, LED15.red_cathode
  N55: IC3.pin3, LED26.green_cathode
  N56: IC3.pin4, LED26.blue_cathode
  N57: IC3.pin5, LED26.red_cathode
  N58: IC3.pin6, LED25.green_cathode
  N59: IC3.pin7, LED25.blue_cathode
  N60: IC3.pin8, LED25.red_cathode
  N61: IC3.pin9, LED24.green_cathode
  N62: IC3.pin10, LED24.blue_cathode
  N63: IC3.pin11, LED24.red_cathode
  N64: IC3.pin12, LED23.green_cathode
  N65: IC3.pin13, LED23.blue_cathode
  N66: IC3.pin14, LED23.red_cathode
  N67: IC3.pin15, LED22.green_cathode
  N68: IC3.pin28, LED15.green_cathode
