# Fritzing sketch MicBoard (saved by Fritzing 0.7.0b)
perfboards: 1

parts:
  J1 = Screw terminal - 2 pins [package=THT]
  IC1 = IC, DIP package, 8 pins [chip_label=LM386 spacing=300mil]
  R1 = Resistor [tolerance=±5% resistance=10k package=THT]
  J2 = screw terminal, 3 pins
  MIC1 = Microphone  # not connected
  C1 = Electrolytic Capacitor [capacitance=1µF package="100 mil [THT, electrolytic]"]
  C5 = Ceramic Capacitor [capacitance=4.7nF package="100 mil [THT, multilayer]"]
  R3 = Resistor [tolerance=±5% resistance=10 package=THT]
  C6 = Electrolytic Capacitor [capacitance=10µF package="100 mil [THT, electrolytic]"]
  C7 = Ceramic Capacitor [capacitance=100nF part_number="radio shack 272-1069" package="100 mil [THT, multilayer]"]
  Arduino1 = Arduino  # not connected

nets (from the pcb view):
  N1: J1.pin1, R1.Pin_1, C1.+
  N2: J1.pin2, IC1.pin2, IC1.pin4, J2.pin2, R3.Pin_1, C6.-, C7.0
  N3: IC1.pin3, C1.-
  N4: IC1.pin5, J2.pin3, C5.0
  N5: IC1.pin6, R1.Pin_0, J2.pin1, C7.1
  N6: IC1.pin7, C6.+
  N7: C5.1, R3.Pin_0
