# Fritzing sketch TwoMicTest (saved by Fritzing 0.7.0b)
breadboards: 1

parts:
  MIC1 = Microphone
  MIC2 = Microphone
  C1 = Electrolytic Capacitor [capacitance=10µF package="100 mil [THT, electrolytic]"]
  R1 = Resistor [tolerance=±5% resistance=220 package=THT]
  IC1 = IC, DIP package, 8 pins [chip_label=LM386N spacing=300mil part_number=LM386]
  C2 = Electrolytic Capacitor [capacitance=10µF package="100 mil [THT, electrolytic]"]
  C3 = Ceramic Capacitor [capacitance=100nF part_number="radio shack 272-1069" package="100 mil [THT, multilayer]"]
  Arduino1 = Arduino
  R2 = Resistor [tolerance=±5% resistance=10 package=THT]
  C4 = Ceramic Capacitor [capacitance=4.7nF package="100 mil [THT, multilayer]"]
  IC2 = IC, DIP package, 8 pins [chip_label=LM386N spacing=300mil part_number=LM386]
  C5 = Electrolytic Capacitor [capacitance=10µF package="100 mil [THT, electrolytic]"]
  C6 = Ceramic Capacitor [capacitance=100nF part_number="radio shack 272-1069" package="100 mil [THT, multilayer]"]
  C7 = Ceramic Capacitor [capacitance=4.7nF package="100 mil [THT, multilayer]"]
  R3 = Resistor [tolerance=±5% resistance=10 package=THT]
  C8 = Electrolytic Capacitor [capacitance=10µF package="100 mil [THT, electrolytic]"]
  R4 = Resistor [tolerance=±5% resistance=220 package=THT]
  J1 = Screw terminal - 2 pins [package=THT]
  J2 = Screw terminal - 2 pins [package=THT]
  C9 = Electrolytic Capacitor [capacitance=0.1mF voltage=16V part_number="nichicon B0942 " package="100 mil [THT, electrolytic]"]
  J3 = female pin header, 2 pins [form="♀ (female)"]
  J4 = female pin header, 2 pins [form="♀ (female)"]

nets:
  N1: MIC1.pin1, IC1.pin2, IC1.pin4, C2.-, R2.Pin_1
  N2: MIC1.pin2, C1.+, R1.Pin_1
  N3: MIC2.pin2, C8.+, R4.Pin_1
  N4: C1.-, IC1.pin3
  N5: R1.Pin_0, IC1.pin6, C3.0, Arduino1.+5V, J4.pin1
  N6: IC1.pin5, Arduino1.A0, C4.0
  N7: IC1.pin7, C2.+
  N8: C3.1, Arduino1.GND, J4.pin2
  N9: Arduino1.A2, IC2.pin5, C7.0
  N10: Arduino1.A4, J1.pin2, J3.pin2
  N11: Arduino1.A5, J1.pin1, J3.pin1
  N12: R2.Pin_0, C4.1
  N13: IC2.pin2, IC2.pin4, C5.-, C6.1, R3.Pin_1, J2.pin1, C9.+
  N14: IC2.pin3, C8.-
  N15: IC2.pin6, C6.0, R4.Pin_0, J2.pin2, C9.-
  N16: IC2.pin7, C5.+
  N17: C7.1, R3.Pin_0

notes:
  string of 20 RGB LEDs
  http://www.sparkfun.com/products/11020
  C1,C2,C5,C8 - Radio Shack 272-1025
  http://www.radioshack.com/product/index.jsp?productId=2102509
  C4, C7 - Radio Shack 272-0134
  http://www.radioshack.com/product/index.jsp?productId=2062364
  C3, C6 - Radio Shack 272-1069
  http://www.radioshack.com/product/index.jsp?productId=2103630
  C9 - Nichicon B0942
  http://www.smelectronics.com/
  IC1, IC2 (AmpOp) - Radio Shack 276-1731
  http://www.radioshack.com/product/index.jsp?productId=2062598
  Electret Microphone
  http://www.sparkfun.com/products/8635
