# Fritzing sketch LcdAssembly (saved by Fritzing 0.9.0b)
perfboards: 1

parts:
  U1 = atmega328 [package=dip]
  Y1 = Resonator [frequency="16 Mhz" package=THT]
  C1 = Ceramic Capacitor [capacitance=100nF package="100 mil [THT, multilayer]"]  # not connected
  R1 = Rotary Potentiometer (Small) [maximum_resistance=100kΩ package=THT]  # not connected
  J3 = molex pin header, 5 pins [form=molex]  # not connected
  J1 = molex pin header, 16 pins [form=molex]  # not connected
  J2 = male pin header, 4 pins [form="♂ (male)"]  # not connected

nets:
  N1: U1.XLAT1, Y1.pin_1
  N2: U1.XLAT2, Y1.0
