# Fritzing sketch PhotocellAssembly (saved by Fritzing 0.9.0b)
perfboards: 1

parts:
  J1 = female pin header, 4 pins [form="♀ (female)"]
  R1 = Photocell (LDR) [package=THT]
  R2 = Resistor [tolerance=±5% resistance=10k package=THT]
  R3 = Resistor [tolerance=±5% resistance=330 package=THT]
  LED1 = LED - 5mm [color="Red (633nm)" package="5 mm [THT]"]

nets:
  N1: J1.pin1, R1.pin_0, R2.Pin_0
  N2: J1.pin2, R2.Pin_1, R3.Pin_1
  N3: J1.pin3, R1.pin_1
  N4: J1.pin4, LED1.anode
  N5: R3.Pin_0, LED1.cathode
