# Fritzing sketch PitchAntenna (saved by Fritzing 0.8.5b)
perfboards: 2

parts:
  L1 = Inductor [package="400 mil [THT]"]
  L2 = Inductor [package="400 mil [THT]"]
  L3 = Inductor [package="400 mil [THT]"]
  L4 = Inductor [package="400 mil [THT]"]
  L5 = Inductor [package="400 mil [THT]"]
  L6 = Inductor [package="400 mil [THT]"]
  L7 = Inductor [package="400 mil [THT]"]
  L8 = Inductor [package="400 mil [THT]"]
  D1 = Rectifier Diode [part_number=1N4001 package="300 mil [THT]"]
  U1 = V18ZA2P [package=v18za2p]
  J1 = Screw terminal - 2 pins [package=THT]
  J2 = Screw terminal - 2 pins [package=THT]
  J3 = Screw terminal - 2 pins [package=THT]
  J4 = Screw terminal - 2 pins [package=THT]

nets:
  N1: L1.pin_0, L3.pin_1
  N2: L1.pin_1, L2.pin_0, D1.cathode
  N3: L2.pin_1, J2.pin2
  N4: L3.pin_0, L4.pin_1
  N5: L4.pin_0, J1.pin2
  N6: L5.pin_0, J4.pin1
  N7: L5.pin_1, L6.pin_0
  N8: L6.pin_1, L7.pin_0
  N9: L7.pin_1, L8.pin_0
  N10: L8.pin_1, J3.pin1
  N11: D1.anode, U1.P$1, J2.pin1

notes:
  Volume Antenna
  Pitch Antenna
  L10
  L9
  L8
  L7
  L4
  L1
  L2
  L3
  C12
  D1
  to JP5
  to JP4:
  - Volume Osc. (pin 1)
  - VCA Processor (pin 2)
  to JP4
  pin 2
  pin 1
